// Logisim project single_cycle_processor.circ as structural Verilog: 11 circuits, main circuit SINGLE_CYCLE_PROCESSOR\
// SARTHAK_PANDA_2022CS51217_hamatam Sai Simha Bruhadeeswar RedDY_2022CS1_1600
module SINGLE_CYCLE_PROCESSOR (
  output [31:0] D_out,
  output [31:0] D_out_2
);

  wire ALU_zero, and_1_out, clock_1_out, control_1_aluop0, control_1_aluop1, control_1_alusrc,
       control_1_branch, control_1_memread, control_1_memtoreg, control_1_memwrite, control_1_regwrite,
       reset_out;
  wire [3:0] aluc_control_1_alusel;
  wire [23:0] PC_q_2;
  wire [31:0] adder_1_out, adder_2_out, ALU_result, ImmGen_out_2, multiplexer_1_out, multiplexer_2_out,
       multiplexer_3_out, PC_q, Reg_read_data_1, Reg_read_data_2;

  Register #(.width(32)) PC (
    .D(multiplexer_1_out), .Q({PC_q[31:26], PC_q_2, PC_q[1:0]}), .clk(clock_1_out), .clr(reset_out));  // open: en
  Clock clock_1 (.out(clock_1_out));
  Button reset (.out(reset_out));
  ROM #(.addrWidth(24), .dataWidth(32)) rom_1 (.addr(PC_q_2), .data(D_out), .sel(1'b1));
  Adder #(.width(32)) adder_1 (.a({PC_q[31:26], PC_q_2, PC_q[1:0]}), .b(32'h4), .out(adder_1_out));  // open: cin, cout
  Immediate_Generation ImmGen (.Instruction(D_out), .out_2(ImmGen_out_2));
  control control_1 (
    .INST_6_0(D_out[6:0]), .ALUOp1(control_1_aluop1), .ALUOp0(control_1_aluop0),
    .MemWrite(control_1_memwrite), .Branch(control_1_branch), .MemRead(control_1_memread),
    .RegWrite(control_1_regwrite), .MemtoReg(control_1_memtoreg), .ALUSrc(control_1_alusrc));
  \reg  Reg (
    .Write_Data(multiplexer_3_out), .rs1(D_out[19:15]), .rd(D_out[11:7]), .rs2(D_out[24:20]),
    .Read_Data_1(Reg_read_data_1), .Read_Data_2(Reg_read_data_2), .RegWEn(control_1_regwrite),
    .Clock(clock_1_out), .reset(reset_out));
  aluc_control aluc_control_1 (
    .ALUOP1(control_1_aluop1), .ALUOP0(control_1_aluop0), .INST30(D_out[30]), .INST12(D_out[12]),
    .INST13(D_out[13]), .INST14(D_out[14]), .ALUSel(aluc_control_1_alusel));
  Multiplexer #(.width(32), .enable("false")) multiplexer_1 (
    .in0(adder_1_out), .in1(adder_2_out), .out(multiplexer_1_out), .sel(and_1_out));
  Adder #(.width(32)) adder_2 (
    .a({PC_q[31:26], PC_q_2, PC_q[1:0]}), .b(ImmGen_out_2), .out(adder_2_out));  // open: cin, cout
  and and_1 (and_1_out, control_1_branch, ALU_zero);
  alu ALU (
    .A(Reg_read_data_1), .B(multiplexer_2_out), .ALUSel(aluc_control_1_alusel), .Zero(ALU_zero),
    .Result(ALU_result));  // open: OverFlow
  Multiplexer #(.width(32), .enable("false")) multiplexer_2 (
    .in0(Reg_read_data_2), .in1(ImmGen_out_2), .out(multiplexer_2_out), .sel(control_1_alusrc));
  Multiplexer #(.width(32), .enable("false")) multiplexer_3 (
    .in0(ALU_result), .in1(D_out_2), .out(multiplexer_3_out), .sel(control_1_memtoreg));
  RAM #(.dataWidth(32), .bus("separate")) ram_1 (
    .addr(ALU_result[9:2]), .din(Reg_read_data_2), .data(D_out_2), .str(control_1_memwrite), .sel(1'b1),
    .clk(clock_1_out), .ld(control_1_memread), .clr(reset_out));

  // Notes on the sheet:
  //   contents of rom_1 (hex, n*v repeats v):
  //   538393 712023 128293 140413 48493 50513 8484b3 912023 140413 150513 752333 fe5306e3
  //   Thamatam Sai Simha Bruhadeeswar Reddy(2022CS11600)
  //   Sarthak Panda(2022CS51217)
endmodule

module \reg  (
  input  [31:0] Write_Data,
  input  [4:0] rs1,
  input  [4:0] rd,
  input  [4:0] rs2,
  input  Clock,
  input  RegWEn,
  input  reset,
  output [31:0] Read_Data_1,
  output [31:0] Read_Data_2
);

  wire decoder_1_out1, decoder_1_out2, decoder_1_out5, decoder_1_out6, decoder_1_out7, decoder_1_out8,
       decoder_1_out9, decoder_1_out10;
  wire [31:0] a0_q, demultiplexer_1_out1, demultiplexer_1_out2, demultiplexer_1_out5, demultiplexer_1_out6,
       demultiplexer_1_out7, demultiplexer_1_out8, demultiplexer_1_out9, demultiplexer_1_out10,
       multiplexer_1_out, multiplexer_2_out, multiplexer_3_out, multiplexer_4_out, multiplexer_5_out,
       multiplexer_6_out, multiplexer_7_out, multiplexer_8_out, ra_q, s0_q, s1_q, sp_q, t0_q, t1_q, t2_q,
       zero_q;

  Decoder #(.select(5)) decoder_1 (
    .out1(decoder_1_out1), .out2(decoder_1_out2), .out5(decoder_1_out5), .out6(decoder_1_out6),
    .out7(decoder_1_out7), .out8(decoder_1_out8), .out9(decoder_1_out9), .out10(decoder_1_out10), .sel(rd),
    .en(RegWEn));  // open: out0, out3, out4, out11, out12, out13, out14, out15, out16, out17, out18, out19, out20, out21, out22, out23, out24, out25, out26, out27, out28, out29, out30, out31
  Demultiplexer #(.select(5), .width(32)) demultiplexer_1 (
    .out1(demultiplexer_1_out1), .out2(demultiplexer_1_out2), .out5(demultiplexer_1_out5),
    .out6(demultiplexer_1_out6), .out7(demultiplexer_1_out7), .out8(demultiplexer_1_out8),
    .out9(demultiplexer_1_out9), .out10(demultiplexer_1_out10), .in(Write_Data), .sel(rd), .en(RegWEn));  // open: out0, out3, out4, out11, out12, out13, out14, out15, out16, out17, out18, out19, out20, out21, out22, out23, out24, out25, out26, out27, out28, out29, out30, out31
  Multiplexer #(.width(32), .enable("false")) multiplexer_1 (
    .in0(ra_q), .in1(demultiplexer_1_out1), .out(multiplexer_1_out), .sel(decoder_1_out1));
  Multiplexer #(.width(32), .enable("false")) multiplexer_2 (
    .in0(sp_q), .in1(demultiplexer_1_out2), .out(multiplexer_2_out), .sel(decoder_1_out2));
  Multiplexer #(.width(32), .enable("false")) multiplexer_3 (
    .in0(t0_q), .in1(demultiplexer_1_out5), .out(multiplexer_3_out), .sel(decoder_1_out5));
  Multiplexer #(.width(32), .enable("false")) multiplexer_4 (
    .in0(t1_q), .in1(demultiplexer_1_out6), .out(multiplexer_4_out), .sel(decoder_1_out6));
  Multiplexer #(.width(32), .enable("false")) multiplexer_5 (
    .in0(t2_q), .in1(demultiplexer_1_out7), .out(multiplexer_5_out), .sel(decoder_1_out7));
  Multiplexer #(.width(32), .enable("false")) multiplexer_6 (
    .in0(s0_q), .in1(demultiplexer_1_out8), .out(multiplexer_6_out), .sel(decoder_1_out8));
  Multiplexer #(.width(32), .enable("false")) multiplexer_7 (
    .in0(s1_q), .in1(demultiplexer_1_out9), .out(multiplexer_7_out), .sel(decoder_1_out9));
  Multiplexer #(.width(32), .enable("false")) multiplexer_8 (
    .in0(a0_q), .in1(demultiplexer_1_out10), .out(multiplexer_8_out), .sel(decoder_1_out10));
  Register #(.width(32)) zero (.D({32{1'b0}}), .en(RegWEn), .Q(zero_q), .clk(Clock));  // open: clr
  Register #(.width(32)) ra (.D(multiplexer_1_out), .en(RegWEn), .Q(ra_q), .clk(Clock), .clr(reset));
  Register #(.width(32)) sp (.D(multiplexer_2_out), .en(RegWEn), .Q(sp_q), .clk(Clock), .clr(reset));
  Register #(.width(32)) t0 (.D(multiplexer_3_out), .en(RegWEn), .Q(t0_q), .clk(Clock), .clr(reset));
  Register #(.width(32)) t1 (.D(multiplexer_4_out), .en(RegWEn), .Q(t1_q), .clk(Clock), .clr(reset));
  Register #(.width(32)) t2 (.D(multiplexer_5_out), .en(RegWEn), .Q(t2_q), .clk(Clock), .clr(reset));
  Register #(.width(32)) s0 (.D(multiplexer_6_out), .en(RegWEn), .Q(s0_q), .clk(Clock), .clr(reset));
  Register #(.width(32)) s1 (.D(multiplexer_7_out), .en(RegWEn), .Q(s1_q), .clk(Clock), .clr(reset));
  Register #(.width(32)) a0 (.D(multiplexer_8_out), .en(RegWEn), .Q(a0_q), .clk(Clock), .clr(reset));
  Multiplexer #(.select(5), .width(32), .enable("false")) multiplexer_9 (
    .in0(zero_q), .in1(ra_q), .in2(sp_q), .in5(t0_q), .in6(t1_q), .in7(t2_q), .in8(s0_q), .in9(s1_q),
    .in10(a0_q), .out(Read_Data_1), .sel(rs1));  // open: in3, in4, in11, in12, in13, in14, in15, in16, in17, in18, in19, in20, in21, in22, in23, in24, in25, in26, in27, in28, in29, in30, in31
  Multiplexer #(.select(5), .width(32), .enable("false")) multiplexer_10 (
    .in0(zero_q), .in1(ra_q), .in2(sp_q), .in5(t0_q), .in6(t1_q), .in7(t2_q), .in8(s0_q), .in9(s1_q),
    .in10(a0_q), .out(Read_Data_2), .sel(rs2));  // open: in3, in4, in11, in12, in13, in14, in15, in16, in17, in18, in19, in20, in21, in22, in23, in24, in25, in26, in27, in28, in29, in30, in31
endmodule

module MULT (
  input  [31:0] A,
  input  [31:0] B,
  input  L_U,
  input  Signed,
  output [31:0] Result
);

  wire and_1_out, and_2_out, bitselector_1_out, bitselector_2_out;
  wire [31:0] adder_1_out, adder_2_out, adder_3_out, adder_4_out, adder_5_out, bit_extender_1_out,
       bit_extender_2_out, bit_extender_3_out, bit_extender_4_out, bit_extender_5_out, bit_extender_6_out,
       bit_extender_7_out, bit_extender_8_out, bit_extender_9_out, bit_extender_10_out, multiplexer_1_out,
       multiplexer_3_out, multiplier_1_out, multiplier_2_out, multiplier_3_out, multiplier_4_out,
       multiplier_5_out, subtractor_1_out, subtractor_2_out;

  assign bit_extender_1_out = {{16{1'b0}}, B[15:0]};  // Bit_Extender bit_extender_1
  assign bit_extender_2_out = {{16{1'b0}}, A[15:0]};  // Bit_Extender bit_extender_2
  assign bit_extender_3_out = {{16{1'b0}}, A[31:16]};  // Bit_Extender bit_extender_3
  Multiplier #(.width(32)) multiplier_1 (.a(A), .b(B), .out(multiplier_1_out), .cin({32{1'b0}}));  // open: cout
  assign bit_extender_4_out = {{16{1'b0}}, B[31:16]};  // Bit_Extender bit_extender_4
  Multiplier #(.width(32)) multiplier_2 (
    .a(bit_extender_2_out), .b(bit_extender_1_out), .out(multiplier_2_out), .cin({32{1'b0}}));  // open: cout
  Multiplier #(.width(32)) multiplier_3 (
    .a(bit_extender_2_out), .b(bit_extender_4_out), .out(multiplier_3_out), .cin({32{1'b0}}));  // open: cout
  Multiplier #(.width(32)) multiplier_4 (
    .a(bit_extender_3_out), .b(bit_extender_1_out), .out(multiplier_4_out), .cin({32{1'b0}}));  // open: cout
  Multiplier #(.width(32)) multiplier_5 (
    .a(bit_extender_3_out), .b(bit_extender_4_out), .out(multiplier_5_out), .cin({32{1'b0}}));  // open: cout
  assign bit_extender_5_out = {{16{1'b0}}, multiplier_2_out[31:16]};  // Bit_Extender bit_extender_5
  assign bit_extender_6_out = {{16{1'b0}}, multiplier_3_out[15:0]};  // Bit_Extender bit_extender_6
  assign bit_extender_7_out = {{16{1'b0}}, multiplier_4_out[15:0]};  // Bit_Extender bit_extender_7
  assign bit_extender_8_out = {{16{1'b0}}, multiplier_4_out[31:16]};  // Bit_Extender bit_extender_8
  assign bit_extender_9_out = {{16{1'b0}}, multiplier_3_out[31:16]};  // Bit_Extender bit_extender_9
  Adder #(.width(32)) adder_1 (
    .a(bit_extender_5_out), .b(bit_extender_6_out), .out(adder_1_out), .cin(1'b0));  // open: cout
  Adder #(.width(32)) adder_2 (
    .a(bit_extender_8_out), .b(bit_extender_9_out), .out(adder_2_out), .cin(1'b0));  // open: cout
  Adder #(.width(32)) adder_3 (.a(adder_1_out), .b(bit_extender_7_out), .out(adder_3_out), .cin(1'b0));  // open: cout
  Adder #(.width(32)) adder_4 (.a(adder_2_out), .b(multiplier_5_out), .out(adder_4_out), .cin(1'b0));  // open: cout
  assign bit_extender_10_out = {{16{1'b0}}, adder_3_out[31:16]};  // Bit_Extender bit_extender_10
  BitSelector #(.width(32)) bitselector_1 (.in(A), .out(bitselector_1_out), .sel({5{1'b1}}));
  Adder #(.width(32)) adder_5 (.a(bit_extender_10_out), .b(adder_4_out), .out(adder_5_out), .cin(1'b0));  // open: cout
  Multiplexer #(.width(32), .enable("false")) multiplexer_1 (
    .in0({32{1'b0}}), .in1(B), .out(multiplexer_1_out), .sel(and_1_out));
  and and_1 (and_1_out, bitselector_1_out, Signed);
  BitSelector #(.width(32)) bitselector_2 (.in(B), .out(bitselector_2_out), .sel({5{1'b1}}));
  Multiplexer #(.select(2), .width(32), .enable("false")) multiplexer_2 (
    .in0(multiplier_1_out), .in1(multiplier_1_out), .in2(adder_5_out), .in3(subtractor_2_out), .out(Result),
    .sel({L_U, Signed}));
  Subtractor #(.width(32)) subtractor_1 (
    .a(adder_5_out), .b(multiplexer_1_out), .out(subtractor_1_out), .bin(1'b0));  // open: bout
  Multiplexer #(.width(32), .enable("false")) multiplexer_3 (
    .in0({32{1'b0}}), .in1(A), .out(multiplexer_3_out), .sel(and_2_out));
  and and_2 (and_2_out, bitselector_2_out, Signed);
  Subtractor #(.width(32)) subtractor_2 (
    .a(subtractor_1_out), .b(multiplexer_3_out), .out(subtractor_2_out), .bin(1'b0));  // open: bout
endmodule

module SHIFT (
  input  [31:0] A,
  input  [31:0] B,
  input  L_R,
  input  L_A,
  output [31:0] Result
);

  wire not_1_out, or_1_out;
  wire [1:0] and_2_out;
  wire [31:0] multiplexer_1_out, multiplexer_2_out, not_2_out, shifter_1_out, shifter_2_out, shifter_3_out;

  Shifter #(.width(32)) shifter_1 (.in(A), .\dist (B[4:0]), .out(shifter_1_out));
  Shifter #(.width(32), .shift("ar")) shifter_2 (.in(A), .\dist (B[4:0]), .out(shifter_2_out));
  Shifter #(.width(32), .shift("lr")) shifter_3 (.in(A), .\dist (B[4:0]), .out(shifter_3_out));
  and and_1 (and_2_out[1], L_R, not_1_out);
  Multiplexer #(.select(2), .width(32), .enable("false")) multiplexer_1 (
    .in0(shifter_1_out), .in1(shifter_2_out), .in2(shifter_3_out), .out(multiplexer_1_out), .sel(and_2_out));  // open: in3
  and and_2 (and_2_out[0], L_R, L_A);
  not not_1 (not_1_out, L_A);
  Multiplexer #(.width(32), .enable("false")) multiplexer_2 (
    .in0({32{1'b0}}), .in1(not_2_out), .out(multiplexer_2_out), .sel(and_2_out[0]));
  assign not_2_out = ~{32{1'b0}};  // NOT_Gate not_2, 32 bits wide
  Multiplexer #(.width(32), .enable("false")) multiplexer_3 (
    .in0(multiplexer_1_out), .in1(multiplexer_2_out), .out(Result), .sel(or_1_out));
  or or_1 (or_1_out, B[31], B[30], B[29], B[28], B[27], B[26], B[25], B[24], B[23], B[22], B[21], B[20], B[19], B[18], B[17], B[16], B[15], B[14], B[13], B[12], B[11], B[10], B[9], B[8], B[7], B[6], B[5]);
endmodule

module ADD_SUB (
  input  Cin,
  input  [31:0] A,
  input  [31:0] B,
  output [31:0] Result,
  output Overflow
);

  wire adder_1_cout, adder_2_cout;
  wire [31:0] multiplexer_1_out, not_1_out;

  assign not_1_out = ~B;  // NOT_Gate not_1, 32 bits wide
  Multiplexer #(.width(32), .enable("false")) multiplexer_1 (
    .in0(B), .in1(not_1_out), .out(multiplexer_1_out), .sel(Cin));
  Adder #(.width(31)) adder_1 (
    .a(A[30:0]), .b(multiplexer_1_out[30:0]), .out(Result[30:0]), .cin(Cin), .cout(adder_1_cout));
  Adder #(.width(1)) adder_2 (
    .a(multiplexer_1_out[31]), .b(A[31]), .out(Result[31]), .cin(adder_1_cout), .cout(adder_2_cout));
  xor xor_1 (Overflow, adder_1_cout, adder_2_cout);
endmodule

module alu (
  input  [31:0] A,
  input  [31:0] B,
  input  [3:0] ALUSel,
  output OverFlow,
  output Zero,
  output [31:0] Result
);

  wire add_sub_1_overflow, comparator_1_lt, comparator_2_lt, decoder_1_out0, decoder_1_out1, decoder_1_out2,
       decoder_1_out3, decoder_1_out4, decoder_1_out5, decoder_1_out6, decoder_1_out7, decoder_1_out8,
       decoder_1_out9, decoder_1_out10, decoder_1_out11, decoder_1_out12, decoder_1_out13, decoder_1_out14,
       decoder_1_out15, or_1_out, or_3_out, or_4_out;
  wire [31:0] add_sub_1_result, and_1_out, bit_extender_1_out, bit_extender_2_out, MULT_result, or_2_out,
       SHIFT_result, xor_1_out;

  Decoder #(.select(4), .enable("false")) decoder_1 (
    .out0(decoder_1_out0), .out1(decoder_1_out1), .out2(decoder_1_out2), .out3(decoder_1_out3),
    .out4(decoder_1_out4), .out5(decoder_1_out5), .out6(decoder_1_out6), .out7(decoder_1_out7),
    .out8(decoder_1_out8), .out9(decoder_1_out9), .out10(decoder_1_out10), .out11(decoder_1_out11),
    .out12(decoder_1_out12), .out13(decoder_1_out13), .out14(decoder_1_out14), .out15(decoder_1_out15),
    .sel(ALUSel));
  or or_1 (or_1_out, decoder_1_out5, decoder_1_out13);
  SHIFT SHIFT (.L_R(or_1_out), .L_A(decoder_1_out13), .A(A), .B(B), .Result(SHIFT_result));
  assign or_2_out = A | B;  // OR_Gate or_2, 32 bits wide
  assign and_1_out = A & B;  // AND_Gate and_1, 32 bits wide
  assign xor_1_out = A ^ B;  // XOR_Gate xor_1, 32 bits wide
  Comparator #(.width(32), .mode("unsigned")) comparator_1 (.a(A), .b(B), .lt(comparator_1_lt));  // open: gt, eq
  or or_3 (or_3_out, decoder_1_out12, decoder_1_out2);
  ADD_SUB add_sub_1 (.Cin(or_3_out), .A(A), .B(B), .Result(add_sub_1_result), .Overflow(add_sub_1_overflow));
  MULT MULT (.A(A), .B(B), .L_U(or_4_out), .Signed(decoder_1_out9), .Result(MULT_result));
  or or_4 (or_4_out, decoder_1_out9, decoder_1_out11);
  Comparator #(.width(32)) comparator_2 (.a(A), .b(B), .lt(comparator_2_lt));  // open: gt, eq
  assign bit_extender_1_out = {{31{1'b0}}, comparator_1_lt};  // Bit_Extender bit_extender_1
  assign bit_extender_2_out = {{31{1'b0}}, comparator_2_lt};  // Bit_Extender bit_extender_2
  Multiplexer #(.select(4), .width(32), .enable("false")) multiplexer_1 (
    .in0(add_sub_1_result), .in1(SHIFT_result), .in2(bit_extender_2_out), .in3(bit_extender_1_out),
    .in4(xor_1_out), .in5(SHIFT_result), .in6(or_2_out), .in7(and_1_out), .in8(MULT_result),
    .in9(MULT_result), .in11(MULT_result), .in12(add_sub_1_result), .in13(SHIFT_result), .in15(B),
    .out(Result), .sel(ALUSel));  // open: in10, in14
  nor nor_1 (Zero, Result[0], Result[1], Result[2], Result[3], Result[4], Result[5], Result[6], Result[7], Result[8], Result[9], Result[10], Result[11], Result[12], Result[13], Result[14], Result[15], Result[17], Result[18], Result[19], Result[20], Result[21], Result[22], Result[23], Result[24], Result[25], Result[26], Result[27], Result[28], Result[29], Result[30], Result[31], Result[16]);
  and and_2 (OverFlow, add_sub_1_overflow, decoder_1_out0);
endmodule

// Control
module control (
  input  [6:0] INST_6_0,
  output ALUOp1,
  output ALUOp0,
  output MemWrite,
  output Branch,
  output MemRead,
  output RegWrite,
  output MemtoReg,
  output ALUSrc
);

  wire I_out, not_1_out, not_2_out, not_3_out, not_4_out, not_5_out, not_6_out, not_7_out, not_8_out,
       not_9_out, R_out;

  not not_1 (not_1_out, INST_6_0[5]);
  not not_2 (not_2_out, INST_6_0[6]);
  and I (I_out, not_2_out, not_1_out, INST_6_0[4]);
  not not_3 (not_3_out, INST_6_0[5]);
  not not_4 (not_4_out, INST_6_0[6]);
  not not_5 (not_5_out, INST_6_0[6]);
  not not_6 (not_6_out, INST_6_0[4]);
  and R (R_out, not_5_out, INST_6_0[5], INST_6_0[4]);
  and lw (MemRead, not_4_out, not_3_out, not_6_out);
  not not_7 (not_7_out, INST_6_0[6]);
  not not_8 (not_8_out, INST_6_0[4]);
  not not_9 (not_9_out, INST_6_0[4]);
  and beq (Branch, INST_6_0[6], INST_6_0[5], not_9_out);
  and sw (MemWrite, not_7_out, INST_6_0[5], not_8_out);
  or or_1 (RegWrite, MemRead, R_out, I_out);
  or or_2 (ALUSrc, MemWrite, MemRead, I_out);
  or or_3 (ALUOp0, INST_6_0[6], I_out);

  assign ALUOp1 = INST_6_0[4];
  assign MemtoReg = MemRead;
endmodule

// IM
module Instruction_memory (
  input  [23:0] A,
  output [31:0] D
);

  ROM #(.addrWidth(24), .dataWidth(32)) rom_1 (.addr(A), .data(D), .sel(1'b1));

  // Notes on the sheet:
  //   contents of rom_1 (hex, n*v repeats v):
  //   1700393 4e00313 734333 32023
endmodule

// ALUCON
module aluc_control (
  input  ALUOP1,
  input  ALUOP0,
  input  INST30,
  input  INST12,
  input  INST13,
  input  INST14,
  output [3:0] ALUSel
);

  wire and_1_out, and_2_out, and_3_out, not_1_out, not_2_out, not_3_out, not_4_out, or_1_out;

  not not_1 (not_1_out, ALUOP1);
  and and_1 (and_1_out, not_1_out, not_2_out);
  not not_2 (not_2_out, ALUOP0);
  not not_3 (not_3_out, ALUOP1);
  and and_2 (and_2_out, not_3_out, ALUOP0);
  not not_4 (not_4_out, ALUOP0);
  and and_3 (and_3_out, ALUOP1, not_4_out, INST30);
  or or_1 (or_1_out, and_2_out, and_3_out);
  or or_2 (ALUSel[2], or_1_out, INST14);
  or or_3 (ALUSel[3], or_1_out, 1'b0);
  Multiplexer #(.enable("false")) multiplexer_1 (.in0(INST13), .in1(1'b0), .out(ALUSel[1]), .sel(and_1_out));

  assign ALUSel[0] = INST12;
endmodule

module Immediate_Generation (
  input  [31:0] Instruction,
  output [31:0] out_2
);

  wire not_1_out;
  wire [31:0] bit_extender_1_out, bit_extender_2_out, bit_extender_3_out, multiplexer_1_out;

  assign bit_extender_1_out = {{19{Instruction[31]}}, {Instruction[31], Instruction[7], Instruction[30:25], Instruction[11:8], 1'b0}};  // Bit_Extender bit_extender_1
  assign bit_extender_2_out = {{20{Instruction[31]}}, Instruction[31:20]};  // Bit_Extender bit_extender_2
  assign bit_extender_3_out = {{20{Instruction[31]}}, {Instruction[31:25], Instruction[11:7]}};  // Bit_Extender bit_extender_3
  Multiplexer #(.width(32), .enable("false")) multiplexer_1 (
    .in0(bit_extender_3_out), .in1(bit_extender_1_out), .out(multiplexer_1_out), .sel(Instruction[6]));
  not not_1 (not_1_out, Instruction[5]);
  Multiplexer #(.width(32), .enable("false")) multiplexer_2 (
    .in0(multiplexer_1_out), .in1(bit_extender_2_out), .out(out_2), .sel(not_1_out));
endmodule

// DM
module Data_memory (
  input  [7:0] A,
  input  [31:0] D_in,
  input  str,
  input  ld,
  input  Clock,
  output [31:0] D_out
);

  RAM #(.dataWidth(32), .bus("separate")) ram_1 (
    .addr(A), .din(D_in), .data(D_out), .str(str), .clk(Clock), .ld(ld));  // open: sel, clr
endmodule
